// Logisim project ch.circ as structural Verilog: 14 circuits, main circuit main
module main (
  input  in_1,
  input  in_2,
  input  [31:0] in_3,
  output [31:0] finaldata
);

  wire clock_1_out;
  wire [31:0] adder_1_out, divider_1_out, ram_1_data, register_1_q;

  Adder #(.width(32)) adder_1 (.a(register_1_q), .b(32'h4), .out(adder_1_out));  // open: cin, cout
  Register #(.width(32)) register_1 (.D(adder_1_out), .en(in_1), .Q(register_1_q), .clk(clock_1_out), .clr(in_2));
  Clock clock_1 (.out(clock_1_out));
  Divider #(.width(32)) divider_1 (.a(register_1_q), .b(in_3), .out(divider_1_out));  // open: upper, rem
  RAM #(.addrWidth(24), .dataWidth(32)) ram_1 (
    .addr(divider_1_out[23:0]), .data(ram_1_data), .clk(clock_1_out));  // open: sel, ld, clr
  imm_datapath imm_datapath_1 (.ins(ram_1_data), .clk(clock_1_out), .datab(finaldata));
endmodule

module rtype (
  input  [31:0] instruction32bit,
  output [6:0] oopcode,
  output [4:0] rd,
  output [2:0] funct3,
  output [4:0] rs1,
  output [4:0] rs2,
  output [6:0] funct7
);


  assign funct3 = instruction32bit[14:12];
  assign funct7 = instruction32bit[31:25];
  assign oopcode = instruction32bit[6:0];
  assign rd = instruction32bit[11:7];
  assign rs1 = instruction32bit[19:15];
  assign rs2 = instruction32bit[24:20];
endmodule

module immediategen (
  input  [31:0] in_1,
  output [31:0] out_2
);

  wire comparator_1_eq, comparator_2_eq, comparator_3_eq, comparator_4_eq, comparator_5_eq, comparator_6_eq;
  wire [2:0] priority_encoder_1_out;
  wire [6:0] i_type_imm_1_oopcode, rtype_1_oopcode, s_type_imm_1_oopcode, sb_type_imm_1_oopcode,
       u_type_imm_1_oopcode, uj_type_imm_1_oopcode;
  wire [31:0] i_imm, s_imm, sb_imm, u_imm, uj_imm;

  rtype rtype_1 (.instruction32bit(in_1), .oopcode(rtype_1_oopcode));  // open: rd, funct3, rs1, rs2, funct7
  i_type_imm i_type_imm_1 (.in_1(in_1), .oopcode(i_type_imm_1_oopcode), .i_imm(i_imm));  // open: rd, funct3, rs1
  s_type_imm s_type_imm_1 (.in_1(in_1), .oopcode(s_type_imm_1_oopcode), .s_imm(s_imm));  // open: funct3, rs1, rs2
  sb_type_imm sb_type_imm_1 (.in_1(in_1), .oopcode(sb_type_imm_1_oopcode), .sb_imm(sb_imm));  // open: funct3, rs1, rs2
  u_type_imm u_type_imm_1 (.in_1(in_1), .oopcode(u_type_imm_1_oopcode), .u_imm(u_imm));  // open: rd
  uj_type_imm uj_type_imm_1 (.in_1(in_1), .oopcode(uj_type_imm_1_oopcode), .uj_imm(uj_imm));  // open: rd
  Comparator #(.width(7)) comparator_1 (
    .a(i_type_imm_1_oopcode), .b(7'b0010011), .eq(comparator_1_eq));  // open: gt, lt
  Comparator #(.width(7)) comparator_2 (
    .a(s_type_imm_1_oopcode), .b(7'b0100011), .eq(comparator_2_eq));  // open: gt, lt
  Comparator #(.width(7)) comparator_3 (
    .a(sb_type_imm_1_oopcode), .b(7'b1100011), .eq(comparator_3_eq));  // open: gt, lt
  Comparator #(.width(7)) comparator_4 (
    .a(u_type_imm_1_oopcode), .b(7'b0110111), .eq(comparator_4_eq));  // open: gt, lt
  Comparator #(.width(7)) comparator_5 (
    .a(uj_type_imm_1_oopcode), .b(7'b1101111), .eq(comparator_5_eq));  // open: gt, lt
  Comparator #(.width(7)) comparator_6 (.a(rtype_1_oopcode), .b(7'b0110011), .eq(comparator_6_eq));  // open: gt, lt
  Multiplexer #(.select(3), .width(32)) multiplexer_1 (
    .in0(i_imm), .in1(s_imm), .in2(sb_imm), .in3(u_imm), .in4(uj_imm), .in5({32{1'b0}}), .out(out_2),
    .sel(priority_encoder_1_out));  // open: in6, in7, en
  Priority_Encoder priority_encoder_1 (
    .in0(comparator_1_eq), .in1(comparator_2_eq), .in2(comparator_3_eq), .in3(comparator_4_eq),
    .in4(comparator_5_eq), .in5(comparator_6_eq), .out(priority_encoder_1_out));  // open: in6, in7, en_in, gs, en_out

  // Other names for the same wires on the sheet: input[31:0] = in_1
endmodule

module registerfile (
  input  [4:0] RS1,
  input  [4:0] RS2,
  input  [4:0] RDI,
  input  clk,
  input  wr,
  input  [31:0] RDvalue,
  output [31:0] rs1out,
  output [31:0] rs2out
);

  wire x0, x1, x2, x3, x4, x5, x6, x7, x8, x9, x10, x11, x12, x13, x14, x15, x16, x17, x18, x19, x20, x21,
       x22, x23, x24, x25, x26, x27, x28, x29, x30, x31;
  wire [31:0] _14out, x0out, x1out, x2out, x3out, x4out, x5out, x6out, x7out, x8out, x9out, x10out, x11out,
       x12out, x13out, x14out, x15out, x16out, x17out, x18out, x19out, x20out, x21out, x22out, x23out,
       x24out, x25out, x26out, x27out, x28out, x29out, x30out, x31out, x170ot;

  Demultiplexer #(.select(5)) demultiplexer_1 (
    .out0(x0), .out1(x1), .out2(x2), .out3(x3), .out4(x4), .out5(x5), .out6(x6), .out7(x7), .out8(x8),
    .out9(x9), .out10(x10), .out11(x11), .out12(x12), .out13(x13), .out14(x14), .out15(x15), .out16(x16),
    .out17(x17), .out18(x18), .out19(x19), .out20(x20), .out21(x21), .out22(x22), .out23(x23), .out24(x24),
    .out25(x25), .out26(x26), .out27(x27), .out28(x28), .out29(x29), .out30(x30), .out31(x31), .in(wr),
    .sel(RDI));  // open: en
  Register #(.width(32)) u_x0 (.D(RDvalue), .en(x0), .Q(x0out), .clk(clk));  // open: clr
  Register #(.width(32)) x0_2 (.D(RDvalue), .en(x4), .Q(x4out), .clk(clk));  // open: clr
  Register #(.width(32)) x0_3 (.D(RDvalue), .en(x8), .Q(x8out), .clk(clk));  // open: clr
  Register #(.width(32)) x0_4 (.D(RDvalue), .en(x12), .Q(x12out), .clk(clk));  // open: clr
  Register #(.width(32)) x0_5 (.D(RDvalue), .en(x16), .Q(x16out), .clk(clk));  // open: clr
  Register #(.width(32)) x0_6 (.D(RDvalue), .en(x20), .Q(x20out), .clk(clk));  // open: clr
  Register #(.width(32)) x0_7 (.D(RDvalue), .en(x24), .Q(x24out), .clk(clk));  // open: clr
  Register #(.width(32)) x0_8 (.D(RDvalue), .en(x28), .Q(x28out), .clk(clk));  // open: clr
  Register #(.width(32)) x0_9 (.D(RDvalue), .en(x1), .Q(x1out), .clk(clk));  // open: clr
  Register #(.width(32)) x0_10 (.D(RDvalue), .en(x5), .Q(x5out), .clk(clk));  // open: clr
  Register #(.width(32)) x0_11 (.D(RDvalue), .en(x9), .Q(x9out), .clk(clk));  // open: clr
  Register #(.width(32)) x0_12 (.D(RDvalue), .en(x13), .Q(x13out), .clk(clk));  // open: clr
  Register #(.width(32)) x0_13 (.D(RDvalue), .en(x17), .Q(x17out), .clk(clk));  // open: clr
  Register #(.width(32)) x0_14 (.D(RDvalue), .en(x21), .Q(x21out), .clk(clk));  // open: clr
  Register #(.width(32)) x0_15 (.D(RDvalue), .en(x25), .Q(x25out), .clk(clk));  // open: clr
  Register #(.width(32)) x0_16 (.D(RDvalue), .en(x29), .Q(x29out), .clk(clk));  // open: clr
  Register #(.width(32)) x0_17 (.D(RDvalue), .en(x2), .Q(x2out), .clk(clk));  // open: clr
  Register #(.width(32)) x0_18 (.D(RDvalue), .en(x6), .Q(x6out), .clk(clk));  // open: clr
  Register #(.width(32)) x0_19 (.D(RDvalue), .en(x10), .Q(x10out), .clk(clk));  // open: clr
  Register #(.width(32)) x0_20 (.D(RDvalue), .en(x14), .Q(x14out), .clk(clk));  // open: clr
  Register #(.width(32)) x0_21 (.D(RDvalue), .en(x18), .Q(x18out), .clk(clk));  // open: clr
  Register #(.width(32)) x0_22 (.D(RDvalue), .en(x22), .Q(x22out), .clk(clk));  // open: clr
  Register #(.width(32)) x0_23 (.D(RDvalue), .en(x26), .Q(x26out), .clk(clk));  // open: clr
  Register #(.width(32)) x0_24 (.D(RDvalue), .en(x30), .Q(x30out), .clk(clk));  // open: clr
  Register #(.width(32)) x0_25 (.D(RDvalue), .en(x3), .Q(x3out), .clk(clk));  // open: clr
  Register #(.width(32)) x0_26 (.D(RDvalue), .en(x7), .Q(x7out), .clk(clk));  // open: clr
  Register #(.width(32)) x0_27 (.D(RDvalue), .en(x11), .Q(x11out), .clk(clk));  // open: clr
  Register #(.width(32)) x0_28 (.D(RDvalue), .en(x15), .Q(x15out), .clk(clk));  // open: clr
  Register #(.width(32)) x0_29 (.D(RDvalue), .en(x19), .Q(x19out), .clk(clk));  // open: clr
  Register #(.width(32)) x0_30 (.D(RDvalue), .en(x23), .Q(x23out), .clk(clk));  // open: clr
  Register #(.width(32)) x0_31 (.D(RDvalue), .en(x27), .Q(x27out), .clk(clk));  // open: clr
  Register #(.width(32)) x0_32 (.D(RDvalue), .en(x31), .Q(x31out), .clk(clk));  // open: clr
  Multiplexer #(.select(5), .width(32)) multiplexer_1 (
    .in0(x0out), .in1(x1out), .in2(x2out), .in3(x3out), .in4(x4out), .in5(x5out), .in6(x6out), .in7(x7out),
    .in8(x8out), .in9(x9out), .in10(x10out), .in11(x11out), .in12(x12out), .in13(x13out), .in14(_14out),
    .in15(x15out), .in16(x16out), .in17(x170ot), .in18(x18out), .in19(x19out), .in20(x20out), .in21(x21out),
    .in22(x22out), .in23(x23out), .in24(x24out), .in25(x25out), .in26(x26out), .in27(x27out), .in28(x28out),
    .in30(x31out), .in31(x31out), .out(rs1out), .sel(RS1));  // open: in29, en
  Multiplexer #(.select(5), .width(32)) multiplexer_2 (
    .in0(x0out), .in1(x1out), .in2(x2out), .in3(x3out), .in4(x4out), .in5(x5out), .in6(x6out), .in7(x7out),
    .in8(x8out), .in9(x9out), .in10(x10out), .in11(x11out), .in12(x12out), .in13(x13out), .in14(_14out),
    .in15(x15out), .in16(x16out), .in17(x170ot), .in18(x18out), .in19(x19out), .in20(x20out), .in21(x21out),
    .in22(x22out), .in23(x23out), .in24(x24out), .in25(x25out), .in26(x26out), .in27(x27out), .in28(x28out),
    .in30(x31out), .in31(x31out), .out(rs2out), .sel(RS2));  // open: in29, en
endmodule

module controllogic (
  input  [31:0] ins,
  output [3:0] sel,
  output wr
);

  wire add, addi, addr, \and , andi, andr, \or , ori, orr, sll, slli, sllr, slt, slti, sltr, sltu, sltui,
       sltur, sra, srai, srar, srl, srli, srlr, sub, \xor , xori, xorr;

  and and_1 (addr, ~ins[2], ~ins[3], ins[4], ins[5], ~ins[6], ~ins[12], ~ins[13], ~ins[14], ~ins[30]);  // AND_Gate
  and and_2 (sub, ~ins[2], ~ins[3], ins[4], ins[5], ~ins[6], ~ins[12], ~ins[13], ~ins[14], ins[30]);  // AND_Gate
  and and_3 (sllr, ~ins[2], ~ins[3], ins[4], ins[5], ~ins[6], ins[12], ~ins[13], ~ins[14], ~ins[30]);  // AND_Gate
  and and_4 (sltr, ~ins[2], ~ins[3], ins[4], ins[5], ~ins[6], ins[12], ins[13], ~ins[14], ~ins[30]);  // AND_Gate
  and and_5 (sltur, ~ins[2], ~ins[3], ins[4], ins[5], ~ins[6], ins[12], ins[13], ~ins[14], ~ins[30]);  // AND_Gate
  and and_6 (xorr, ~ins[2], ~ins[3], ins[4], ins[5], ~ins[6], ins[12], ~ins[13], ins[14]);  // AND_Gate
  and and_7 (srlr, ~ins[2], ~ins[3], ins[4], ins[5], ~ins[6], ins[12], ~ins[13], ins[14], ~ins[30]);  // AND_Gate
  and and_8 (srar, ~ins[2], ~ins[3], ins[4], ins[5], ~ins[6], ins[12], ~ins[13], ins[14], ins[30]);  // AND_Gate
  and and_9 (orr, ~ins[2], ~ins[3], ins[4], ins[5], ~ins[6], ins[12], ins[13], ins[14], ~ins[30]);  // AND_Gate
  and and_10 (andr, ~ins[2], ~ins[3], ins[4], ins[5], ~ins[6], ins[12], ins[13], ins[14], ~ins[30]);  // AND_Gate
  or or_1 (sel[3], sub, sra);
  or or_2 (sel[2], \xor , srl, sra, \or , \and );
  or or_3 (sel[1], slt, sltu, \or , \and );
  or or_4 (sel[0], sll, sltu, srl, sra, \and );
  or or_5 (wr, add, sub, sll, slt, sltu, \xor , srl, sra, \or , \and );
  or or_6 (add, addr, addi);
  or or_7 (slt, sltr, slti);
  or or_8 (sltu, sltur, sltui);
  or or_9 (\xor , xorr, xori);
  or or_10 (srl, srlr, srli);
  or or_11 (sra, srar, srai);
  and and_11 (addi, ~ins[2], ~ins[3], ins[4], ~ins[5], ~ins[6], ~ins[12], ~ins[13], ~ins[14], ~ins[30]);  // AND_Gate
  and and_12 (slli, ~ins[2], ~ins[3], ins[4], ~ins[5], ~ins[6], ins[12], ~ins[13], ~ins[14], ~ins[30]);  // AND_Gate
  or or_12 (sll, sllr, slli);
  and and_13 (slti, ~ins[2], ~ins[3], ins[4], ~ins[5], ~ins[6], ~ins[12], ins[13], ~ins[14], ~ins[30]);  // AND_Gate
  and and_14 (sltui, ~ins[2], ~ins[3], ins[4], ~ins[5], ~ins[6], ins[12], ins[13], ~ins[14], ~ins[30]);  // AND_Gate
  and and_15 (xori, ~ins[2], ~ins[3], ins[4], ~ins[5], ~ins[6], ~ins[12], ~ins[13], ins[14], ~ins[30]);  // AND_Gate
  and and_16 (srli, ~ins[2], ~ins[3], ins[4], ~ins[5], ~ins[6], ins[12], ~ins[13], ins[14], ~ins[30]);  // AND_Gate
  and and_17 (srai, ~ins[2], ~ins[3], ins[4], ~ins[5], ~ins[6], ins[12], ~ins[13], ins[14], ins[30]);  // AND_Gate
  or or_13 (\and , andr, andi);
  and and_18 (ori, ~ins[2], ~ins[3], ins[4], ~ins[5], ~ins[6], ins[12], ins[13], ~ins[14], ~ins[30]);  // AND_Gate
  or or_14 (\or , orr, ori);
  and and_19 (andi, ~ins[2], ~ins[3], ins[4], ~ins[5], ~ins[6], ins[12], ins[13], ins[14], ~ins[30]);  // AND_Gate

  // Other names for the same wires on the sheet: i0 = ins[2]; i1 = ins[3]; i2 = ins[4]; i3 = ins[5]; i4 = ins[6];
  //   i5 = ins[12]; i6 = ins[13]; i7 = ins[14]; i8 = ins[30]; out0 = sel[0]; out1 = sel[1]; out2 = sel[2];
  //   out3 = sel[3]
endmodule

module i_type_imm (
  input  [31:0] in_1,
  output [6:0] oopcode,
  output [4:0] rd,
  output [2:0] funct3,
  output [4:0] rs1,
  output [31:0] i_imm
);

  assign i_imm = {{20{1'b0}}, in_1[31:20]};  // Bit_Extender bit_extender_1

  assign funct3 = in_1[14:12];
  assign oopcode = in_1[6:0];
  assign rd = in_1[11:7];
  assign rs1 = in_1[19:15];
endmodule

module s_type_imm (
  input  [31:0] in_1,
  output [6:0] oopcode,
  output [2:0] funct3,
  output [4:0] rs1,
  output [4:0] rs2,
  output [31:0] s_imm
);

  assign s_imm = {{20{1'b0}}, {in_1[31:25], in_1[11:7]}};  // Bit_Extender bit_extender_1

  assign funct3 = in_1[14:12];
  assign oopcode = in_1[6:0];
  assign rs1 = in_1[19:15];
  assign rs2 = in_1[24:20];
endmodule

module sb_type_imm (
  input  [31:0] in_1,
  output [6:0] oopcode,
  output [2:0] funct3,
  output [4:0] rs1,
  output [4:0] rs2,
  output [31:0] sb_imm
);

  assign sb_imm = {{20{1'b0}}, {in_1[31:25], in_1[11:7]}};  // Bit_Extender bit_extender_1

  assign funct3 = in_1[14:12];
  assign oopcode = in_1[6:0];
  assign rs1 = in_1[19:15];
  assign rs2 = in_1[24:20];
endmodule

module u_type_imm (
  input  [31:0] in_1,
  output [6:0] oopcode,
  output [4:0] rd,
  output [31:0] u_imm
);

  assign u_imm = {{12{1'b0}}, in_1[31:12]};  // Bit_Extender bit_extender_1

  assign oopcode = in_1[6:0];
  assign rd = in_1[11:7];
endmodule

module uj_type_imm (
  input  [31:0] in_1,
  output [6:0] oopcode,
  output [4:0] rd,
  output [31:0] uj_imm
);

  assign uj_imm = {{12{1'b0}}, in_1[31:12]};  // Bit_Extender bit_extender_1

  assign oopcode = in_1[6:0];
  assign rd = in_1[11:7];
endmodule

module alu (
  input  [31:0] data1,
  input  [31:0] data2,
  input  [3:0] sel,
  output [31:0] dataD
);

  wire comparator_1_lt, comparator_2_lt;
  wire [31:0] adderOut, andout, orout, sll, slt, sltunsigned, sra, srl, subOut, xorout;

  Adder #(.width(32)) adder_1 (.a(data1), .b(data2), .out(adderOut));  // open: cin, cout
  Subtractor #(.width(32)) subtractor_1 (.a(data1), .b(data2), .out(subOut));  // open: bin, bout
  Shifter #(.width(32)) shifter_1 (.in(data1), .\dist (data2[4:0]), .out(sll));
  Comparator #(.width(32)) comparator_1 (.a(data1), .b(data2), .lt(comparator_1_lt));  // open: gt, eq
  Comparator #(.width(32)) comparator_2 (.a(data1), .b(data2), .lt(comparator_2_lt));  // open: gt, eq
  Shifter #(.width(32), .shift("lr")) shifter_2 (.in(data1), .\dist (data2[4:0]), .out(srl));
  Shifter #(.width(32), .shift("ar")) shifter_3 (.in(data1), .\dist (data2[4:0]), .out(sra));
  assign slt = {{31{1'b0}}, comparator_1_lt};  // Bit_Extender bit_extender_1
  assign sltunsigned = {{31{1'b0}}, comparator_2_lt};  // Bit_Extender bit_extender_2
  assign xorout = data1 ^ data2;  // XOR_Gate xor_1, 32 bits wide
  assign andout = data1 & data2;  // AND_Gate and_1, 32 bits wide
  assign orout = data1 | data2;  // OR_Gate or_1, 32 bits wide
  Multiplexer #(.select(4), .width(32)) multiplexer_1 (
    .in0(adderOut), .in1(sll), .in2(slt), .in3(sltunsigned), .in4(xorout), .in5(srl), .in6(orout),
    .in7(andout), .in8(subOut), .in14(sra), .out(dataD), .sel(sel));  // open: in9, in10, in11, in12, in13, in15, en

  // Other names for the same wires on the sheet: data1i[31:0] = data1; data2i[31:0] = data2;
  //   data2shift[4:0] = data2[4:0]
endmodule

module brancher (
  input  [31:0] data1,
  input  [31:0] data2,
  input  br_unsigned,
  output br_lessthan,
  output bge_u,
  output br_eq
);

  wire comparator_1_gt, comparator_1_lt, comparator_2_eq, comparator_2_gt, comparator_2_lt, or_1_out,
       or_2_out;

  Comparator #(.width(32)) comparator_1 (.a(data1), .b(data2), .gt(comparator_1_gt), .eq(br_eq), .lt(comparator_1_lt));
  Comparator #(.width(32), .mode("unsigned")) comparator_2 (
    .a(data1), .b(data2), .gt(comparator_2_gt), .eq(comparator_2_eq), .lt(comparator_2_lt));
  Multiplexer multiplexer_1 (
    .in0(comparator_1_lt), .in1(comparator_2_lt), .out(br_lessthan), .sel(br_unsigned));  // open: en
  or or_1 (or_1_out, comparator_2_gt, comparator_2_eq);
  or or_2 (or_2_out, comparator_1_gt, br_eq);
  Multiplexer multiplexer_2 (.in0(or_2_out), .in1(or_1_out), .out(bge_u), .sel(br_unsigned));  // open: en

  // Other names for the same wires on the sheet: br_eq_t = br_eq; br_lessthan_t = br_lessthan;
  //   br_unsigned_t = br_unsigned
endmodule

module alucontrolforimmediate (
  input  [31:0] rs2,
  input  [31:0] imm,
  output [31:0] datab
);

  wire [31:0] xor_1_out, xor_2_out;

  assign xor_1_out = rs2 ^ {32{1'b0}};  // XOR_Gate xor_1, 32 bits wide
  assign xor_2_out = {32{1'b0}} ^ imm;  // XOR_Gate xor_2, 32 bits wide
  assign datab = xor_1_out | xor_2_out;  // OR_Gate or_1, 32 bits wide
endmodule

module imm_datapath (
  input  [31:0] ins,
  input  clk,
  output [31:0] datab
);

  wire controllogic_1_wr;
  wire [3:0] controllogic_1_sel;
  wire [31:0] alucontrolforimmediate_1_datab, immediategen_1_out_2, registerfile_1_rs1out,
       registerfile_1_rs2out;

  immediategen immediategen_1 (.in_1(ins), .out_2(immediategen_1_out_2));
  controllogic controllogic_1 (.ins(ins), .sel(controllogic_1_sel), .wr(controllogic_1_wr));
  registerfile registerfile_1 (
    .RS1(ins[19:15]), .RS2(ins[24:20]), .RDI(ins[11:7]), .clk(clk), .wr(controllogic_1_wr), .RDvalue(datab),
    .rs1out(registerfile_1_rs1out), .rs2out(registerfile_1_rs2out));
  alucontrolforimmediate alucontrolforimmediate_1 (
    .rs2(registerfile_1_rs2out), .imm(immediategen_1_out_2), .datab(alucontrolforimmediate_1_datab));
  alu alu_1 (
    .data1(registerfile_1_rs1out), .data2(alucontrolforimmediate_1_datab), .sel(controllogic_1_sel),
    .dataD(datab));

  // Other names for the same wires on the sheet: rdi[4:0] = ins[11:7]; rs1[4:0] = ins[19:15]; rs2[4:0] = ins[24:20]
endmodule
